# Fritzing sketch EdgeDeviceArduinoNano (saved by Fritzing 0.9.3b)
circuit board: 9.04382cm x 6.46399cm
perfboards: 1

parts:
  Part2 = NRF24L01+ Breakout Board
  U4 = TLP621 [package=THT]
  R5 = Resistor [tolerance=±5% resistance=220 package=THT]
  Part3 = Arduino Nano (Rev3.0)
  R6 = Resistor [tolerance=±5% resistance=150 package=THT]
  C1 = Electrolytic Capacitor [capacitance=10µF package="100 mil [THT, electrolytic]"]
  R7 = Resistor [tolerance=±5% resistance=220 package=THT]
  JP2 = Header 2 [package=molex-1x2_lock]
  LED1 = LED - 5mm [color="Green (565nm)" package="5 mm [THT]"]
  U5 = Hirose DF13 Series Header [part_number="VIN 7 -18v" package=DF13A-2P-1.25H]

nets:
  N1: Part2.GND, C1.-
  VCC: Part2.VCC, Part3.3V3, C1.+
  N2: Part2.CE, Part3.D9
  N3: Part2.CS, Part3.D10
  N4: Part2.SCK, Part3.D13/SCK
  N5: Part2.MOSI, Part3.D11/MOSI
  N6: Part2.MISO, Part3.D12/MISO
  N7: U4.Pin_1, R5.Pin_1
  GND: U4.Pin_2, Part3.GND, LED1.cathode, U5.2
  N8: U4.Pin_4, JP2.2
  N9: U4.Pin_3, JP2.1
  N10: R5.Pin_0, Part3.D2
  N11: Part3.D3, R7.Pin_0
  N12: Part3.VIN, R6.Pin_1
  N13: R6.Pin_0, U5.1
  N14: R7.Pin_1, LED1.anode
